// Logisim project cpu.circ as structural Verilog
module _16_bit_register (
  input  [15:0] \input ,
  input  clk,
  input  WE,
  input  RES,
  output [15:0] \output 
);

  D_Flip_Flop d_ff_1 (.clk(clk), .D(\input [0]), .Q(\output [0]), .en(WE), .reset(RES));  // open: Qn, preset
  D_Flip_Flop d_ff_2 (.clk(clk), .D(\input [1]), .Q(\output [1]), .en(WE), .reset(RES));  // open: Qn, preset
  D_Flip_Flop d_ff_3 (.clk(clk), .D(\input [2]), .Q(\output [2]), .en(WE), .reset(RES));  // open: Qn, preset
  D_Flip_Flop d_ff_4 (.clk(clk), .D(\input [3]), .Q(\output [3]), .en(WE), .reset(RES));  // open: Qn, preset
  D_Flip_Flop d_ff_5 (.clk(clk), .D(\input [4]), .Q(\output [4]), .en(WE), .reset(RES));  // open: Qn, preset
  D_Flip_Flop d_ff_6 (.clk(clk), .D(\input [5]), .Q(\output [5]), .en(WE), .reset(RES));  // open: Qn, preset
  D_Flip_Flop d_ff_7 (.clk(clk), .D(\input [6]), .Q(\output [6]), .en(WE), .reset(RES));  // open: Qn, preset
  D_Flip_Flop d_ff_8 (.clk(clk), .D(\input [7]), .Q(\output [7]), .en(WE), .reset(RES));  // open: Qn, preset
  D_Flip_Flop d_ff_9 (.clk(clk), .D(\input [8]), .Q(\output [8]), .en(WE), .reset(RES));  // open: Qn, preset
  D_Flip_Flop d_ff_10 (.clk(clk), .D(\input [9]), .Q(\output [9]), .en(WE), .reset(RES));  // open: Qn, preset
  D_Flip_Flop d_ff_11 (.clk(clk), .D(\input [10]), .Q(\output [10]), .en(WE), .reset(RES));  // open: Qn, preset
  D_Flip_Flop d_ff_12 (.clk(clk), .D(\input [11]), .Q(\output [11]), .en(WE), .reset(RES));  // open: Qn, preset
  D_Flip_Flop d_ff_13 (.clk(clk), .D(\input [12]), .Q(\output [12]), .en(WE), .reset(RES));  // open: Qn, preset
  D_Flip_Flop d_ff_14 (.clk(clk), .D(\input [13]), .Q(\output [13]), .en(WE), .reset(RES));  // open: Qn, preset
  D_Flip_Flop d_ff_15 (.clk(clk), .D(\input [14]), .Q(\output [14]), .en(WE), .reset(RES));  // open: Qn, preset
  D_Flip_Flop d_ff_16 (.clk(clk), .D(\input [15]), .Q(\output [15]), .en(WE), .reset(RES));  // open: Qn, preset

  // Other names for the same wires on the sheet: _0 = \input [0]; _1 = \input [1]; _2 = \input [2]; _3 = \input [3];
  //   _4 = \input [4]; _5 = \input [5]; _6 = \input [6]; _7 = \input [7]; _8 = \input [8]; _9 = \input [9];
  //   _10 = \input [10]; _11 = \input [11]; _12 = \input [12]; _13 = \input [13]; _14 = \input [14];
  //   _15 = \input [15]; Q0 = \output [0]; Q1 = \output [1]; Q2 = \output [2]; Q3 = \output [3]; Q4 = \output [4];
  //   Q5 = \output [5]; Q6 = \output [6]; Q7 = \output [7]; Q8 = \output [8]; Q9 = \output [9]; Q10 = \output [10];
  //   Q11 = \output [11]; Q12 = \output [12]; Q13 = \output [13]; Q14 = \output [14]; Q15 = \output [15]
endmodule

module register_file (
  input  reset,
  input  clk,
  input  [2:0] read1,
  input  [2:0] read2,
  input  RegWriteEnable,
  input  [2:0] write,
  input  [15:0] data,
  output [15:0] out1,
  output [15:0] out2
);

  wire decoder_1_out1, decoder_1_out2, decoder_1_out3, decoder_1_out4, decoder_1_out5, decoder_1_out6,
       decoder_1_out7, decoder_2_out0, decoder_2_out1, decoder_2_out2, decoder_2_out3, decoder_2_out4,
       decoder_2_out5, decoder_2_out6, decoder_2_out7, decoder_3_out0, decoder_3_out1, decoder_3_out2,
       decoder_3_out3, decoder_3_out4, decoder_3_out5, decoder_3_out6, decoder_3_out7;
  wire [15:0] n16_bit_register_1_output, n16_bit_register_2_output, n16_bit_register_3_output,
       n16_bit_register_4_output, n16_bit_register_5_output, n16_bit_register_6_output,
       n16_bit_register_7_output, n16_bit_register_8_output;

  Decoder #(.select(3), .disabled(0)) decoder_1 (
    .out1(decoder_1_out1), .out2(decoder_1_out2), .out3(decoder_1_out3), .out4(decoder_1_out4),
    .out5(decoder_1_out5), .out6(decoder_1_out6), .out7(decoder_1_out7), .sel(write), .en(RegWriteEnable));  // open: out0
  _16_bit_register u_16_bit_register_1 (
    .clk(clk), .RES(reset), .\output (n16_bit_register_1_output));  // open: input, WE
  _16_bit_register u_16_bit_register_2 (
    .\input (data), .clk(clk), .WE(decoder_1_out1), .RES(reset), .\output (n16_bit_register_2_output));
  _16_bit_register u_16_bit_register_3 (
    .\input (data), .clk(clk), .WE(decoder_1_out2), .RES(reset), .\output (n16_bit_register_3_output));
  _16_bit_register u_16_bit_register_4 (
    .\input (data), .clk(clk), .WE(decoder_1_out3), .RES(reset), .\output (n16_bit_register_4_output));
  _16_bit_register u_16_bit_register_5 (
    .\input (data), .clk(clk), .WE(decoder_1_out4), .RES(reset), .\output (n16_bit_register_5_output));
  _16_bit_register u_16_bit_register_6 (
    .\input (data), .clk(clk), .WE(decoder_1_out5), .RES(reset), .\output (n16_bit_register_6_output));
  _16_bit_register u_16_bit_register_7 (
    .\input (data), .clk(clk), .WE(decoder_1_out6), .RES(reset), .\output (n16_bit_register_7_output));
  _16_bit_register u_16_bit_register_8 (
    .\input (data), .clk(clk), .WE(decoder_1_out7), .RES(reset), .\output (n16_bit_register_8_output));
  // Probe on n16_bit_register_1_output
  // Probe on n16_bit_register_2_output
  // Probe on n16_bit_register_3_output
  // Probe on n16_bit_register_4_output
  // Probe on n16_bit_register_5_output
  // Probe on n16_bit_register_6_output
  // Probe on n16_bit_register_7_output
  // Probe on n16_bit_register_8_output
  assign out2 = decoder_3_out0 ? n16_bit_register_1_output : 16'bz;  // Controlled_Buffer controlled_buffer_1
  assign out1 = decoder_2_out0 ? n16_bit_register_1_output : 16'bz;  // Controlled_Buffer controlled_buffer_2
  assign out2 = decoder_3_out1 ? n16_bit_register_2_output : 16'bz;  // Controlled_Buffer controlled_buffer_3
  assign out1 = decoder_2_out1 ? n16_bit_register_2_output : 16'bz;  // Controlled_Buffer controlled_buffer_4
  assign out2 = decoder_3_out2 ? n16_bit_register_3_output : 16'bz;  // Controlled_Buffer controlled_buffer_5
  assign out1 = decoder_2_out2 ? n16_bit_register_3_output : 16'bz;  // Controlled_Buffer controlled_buffer_6
  assign out2 = decoder_3_out3 ? n16_bit_register_4_output : 16'bz;  // Controlled_Buffer controlled_buffer_7
  assign out1 = decoder_2_out3 ? n16_bit_register_4_output : 16'bz;  // Controlled_Buffer controlled_buffer_8
  assign out2 = decoder_3_out4 ? n16_bit_register_5_output : 16'bz;  // Controlled_Buffer controlled_buffer_9
  assign out1 = decoder_2_out4 ? n16_bit_register_5_output : 16'bz;  // Controlled_Buffer controlled_buffer_10
  assign out2 = decoder_3_out5 ? n16_bit_register_6_output : 16'bz;  // Controlled_Buffer controlled_buffer_11
  assign out1 = decoder_2_out5 ? n16_bit_register_6_output : 16'bz;  // Controlled_Buffer controlled_buffer_12
  assign out2 = decoder_3_out6 ? n16_bit_register_7_output : 16'bz;  // Controlled_Buffer controlled_buffer_13
  assign out1 = decoder_2_out6 ? n16_bit_register_7_output : 16'bz;  // Controlled_Buffer controlled_buffer_14
  assign out2 = decoder_3_out7 ? n16_bit_register_8_output : 16'bz;  // Controlled_Buffer controlled_buffer_15
  assign out1 = decoder_2_out7 ? n16_bit_register_8_output : 16'bz;  // Controlled_Buffer controlled_buffer_16
  Decoder #(.select(3), .disabled(0), .enable("false")) decoder_2 (
    .out0(decoder_2_out0), .out1(decoder_2_out1), .out2(decoder_2_out2), .out3(decoder_2_out3),
    .out4(decoder_2_out4), .out5(decoder_2_out5), .out6(decoder_2_out6), .out7(decoder_2_out7), .sel(read1));
  Decoder #(.select(3), .disabled(0), .enable("false")) decoder_3 (
    .out0(decoder_3_out0), .out1(decoder_3_out1), .out2(decoder_3_out2), .out3(decoder_3_out3),
    .out4(decoder_3_out4), .out5(decoder_3_out5), .out6(decoder_3_out6), .out7(decoder_3_out7), .sel(read2));
endmodule

module full_adder (
  input  sub,
  input  [15:0] A,
  input  [15:0] B,
  output [15:0] result,
  output ovf
);

  wire n1_bit_adder_1_cout, n1_bit_adder_2_cout, n1_bit_adder_3_cout, n1_bit_adder_4_cout,
       n1_bit_adder_5_cout, n1_bit_adder_6_cout, n1_bit_adder_7_cout, n1_bit_adder_8_cout,
       n1_bit_adder_9_cout, n1_bit_adder_10_cout, n1_bit_adder_11_cout, n1_bit_adder_12_cout,
       n1_bit_adder_13_cout, n1_bit_adder_14_cout, n1_bit_adder_15_cout, n1_bit_adder_16_cout, xor_1_out,
       xor_2_out, xor_3_out, xor_4_out, xor_5_out, xor_6_out, xor_7_out, xor_8_out, xor_9_out, xor_10_out,
       xor_11_out, xor_12_out, xor_13_out, xor_14_out, xor_15_out, xor_16_out;

  xor xor_1 (xor_1_out, B[0], sub);
  xor xor_2 (xor_2_out, B[1], sub);
  xor xor_3 (xor_3_out, B[2], sub);
  xor xor_4 (xor_4_out, B[3], sub);
  xor xor_5 (xor_5_out, B[4], sub);
  xor xor_6 (xor_6_out, B[5], sub);
  xor xor_7 (xor_7_out, B[6], sub);
  xor xor_8 (xor_8_out, B[7], sub);
  xor xor_9 (xor_9_out, B[8], sub);
  xor xor_10 (xor_10_out, B[9], sub);
  xor xor_11 (xor_11_out, B[10], sub);
  xor xor_12 (xor_12_out, B[11], sub);
  xor xor_13 (xor_13_out, B[12], sub);
  xor xor_14 (xor_14_out, B[13], sub);
  xor xor_15 (xor_15_out, B[14], sub);
  xor xor_16 (xor_16_out, B[15], sub);
  _1_bit_adder u_1_bit_adder_1 (.A(A[0]), .B(xor_1_out), .sum(result[0]), .Cin(sub), .Cout(n1_bit_adder_1_cout));
  _1_bit_adder u_1_bit_adder_2 (
    .A(A[1]), .B(xor_2_out), .sum(result[1]), .Cin(n1_bit_adder_1_cout), .Cout(n1_bit_adder_2_cout));
  _1_bit_adder u_1_bit_adder_3 (
    .A(A[2]), .B(xor_3_out), .sum(result[2]), .Cin(n1_bit_adder_2_cout), .Cout(n1_bit_adder_3_cout));
  _1_bit_adder u_1_bit_adder_4 (
    .A(A[3]), .B(xor_4_out), .sum(result[3]), .Cin(n1_bit_adder_3_cout), .Cout(n1_bit_adder_4_cout));
  _1_bit_adder u_1_bit_adder_5 (
    .A(A[4]), .B(xor_5_out), .sum(result[4]), .Cin(n1_bit_adder_4_cout), .Cout(n1_bit_adder_5_cout));
  _1_bit_adder u_1_bit_adder_6 (
    .A(A[5]), .B(xor_6_out), .sum(result[5]), .Cin(n1_bit_adder_5_cout), .Cout(n1_bit_adder_6_cout));
  _1_bit_adder u_1_bit_adder_7 (
    .A(A[6]), .B(xor_7_out), .sum(result[6]), .Cin(n1_bit_adder_6_cout), .Cout(n1_bit_adder_7_cout));
  _1_bit_adder u_1_bit_adder_8 (
    .A(A[7]), .B(xor_8_out), .sum(result[7]), .Cin(n1_bit_adder_7_cout), .Cout(n1_bit_adder_8_cout));
  _1_bit_adder u_1_bit_adder_9 (
    .A(A[8]), .B(xor_9_out), .sum(result[8]), .Cin(n1_bit_adder_8_cout), .Cout(n1_bit_adder_9_cout));
  _1_bit_adder u_1_bit_adder_10 (
    .A(A[9]), .B(xor_10_out), .sum(result[9]), .Cin(n1_bit_adder_9_cout), .Cout(n1_bit_adder_10_cout));
  _1_bit_adder u_1_bit_adder_11 (
    .A(A[10]), .B(xor_11_out), .sum(result[10]), .Cin(n1_bit_adder_10_cout), .Cout(n1_bit_adder_11_cout));
  _1_bit_adder u_1_bit_adder_12 (
    .A(A[11]), .B(xor_12_out), .sum(result[11]), .Cin(n1_bit_adder_11_cout), .Cout(n1_bit_adder_12_cout));
  _1_bit_adder u_1_bit_adder_13 (
    .A(A[12]), .B(xor_13_out), .sum(result[12]), .Cin(n1_bit_adder_12_cout), .Cout(n1_bit_adder_13_cout));
  _1_bit_adder u_1_bit_adder_14 (
    .A(A[13]), .B(xor_14_out), .sum(result[13]), .Cin(n1_bit_adder_13_cout), .Cout(n1_bit_adder_14_cout));
  _1_bit_adder u_1_bit_adder_15 (
    .A(A[14]), .B(xor_15_out), .sum(result[14]), .Cin(n1_bit_adder_14_cout), .Cout(n1_bit_adder_15_cout));
  _1_bit_adder u_1_bit_adder_16 (
    .A(A[15]), .B(xor_16_out), .sum(result[15]), .Cin(n1_bit_adder_15_cout), .Cout(n1_bit_adder_16_cout));
  xor xor_17 (ovf, n1_bit_adder_15_cout, n1_bit_adder_16_cout);
endmodule

module _1_bit_adder (
  input  Cin,
  input  A,
  input  B,
  output sum,
  output Cout
);

  wire and_1_out, and_2_out, xor_1_out;

  and and_1 (and_1_out, A, B);
  xor xor_1 (xor_1_out, A, B);
  and and_2 (and_2_out, Cin, xor_1_out);
  or or_1 (Cout, and_1_out, and_2_out);
  xor xor_2 (sum, Cin, xor_1_out);
endmodule
